# Fritzing sketch Arduino Estacionamiento (saved by Fritzing 0.9.0b)
breadboards: 1

parts:
  Parte1 = Arduino Uno (Rev3)
  J1 = Basic Servo
  S2 = Pushbutton [package="[THT]"]
  R1 = Resistor [tolerance=±5% resistance=220 package=THT]
  R2 = Resistor [tolerance=±5% resistance=220 package=THT]
  R3 = Resistor [tolerance=±5% resistance=220 package=THT]
  R4 = Resistor [tolerance=±5% resistance=220 package=THT]
  R5 = Resistor [tolerance=±5% resistance=220 package=THT]
  R6 = Resistor [tolerance=±5% resistance=220 package=THT]
  R7 = Resistor [tolerance=±5% resistance=220 package=THT]
  S3 = Pushbutton [package="[THT]"]
  U1 = 7-SEGMENT-DISPLAY [package=7-segment-display]
  R8 = Resistor [tolerance=±5% resistance=220 package=THT]
  R9 = Resistor [tolerance=±5% resistance=220 package=THT]

nets:
  N1: Parte1.D8, R4.Pin_0, U1.E
  N2: Parte1.D9_PWM, J1.pulse
  N3: Parte1.D10_PWM/SS, S3.Pin_1, S3.Pin_2, R8.Pin_0
  N4: Parte1.D11_PWM/MOSI, S2.Pin_3, S2.Pin_4, R9.Pin_0
  N5: Parte1.D2, R6.Pin_0, U1.G2
  N6: Parte1.D3_PWM, R7.Pin_0, U1.A
  N7: Parte1.D4, R3.Pin_1, U1.DP
  N8: Parte1.D5_PWM, R2.Pin_1, U1.G1
  N9: Parte1.D6_PWM, R1.Pin_1, U1.D
  N10: Parte1.D7, R5.Pin_0, U1.G
  5V: Parte1.5V, J1.vcc, S2.Pin_1, S2.Pin_2, R1.Pin_0, R2.Pin_0, R3.Pin_0, R4.Pin_1, R5.Pin_1, R6.Pin_1, R7.Pin_1, S3.Pin_3, S3.Pin_4
  GND: Parte1.GND, J1.gnd, U1.C, U1.F, R8.Pin_1, R9.Pin_1
